# Fritzing sketch SERRA_Appartamento (saved by Fritzing 0.9.3b)
breadboards: 1

parts:
  Componente1 = BluePill
  Mod1 = RYLR896 [package=THT]
  RHT1 = Humidity and Temperature Sensor RHT03
  Bauteil4 = Barometric Pressure Sensor - BMP085 Breakout
  Componente2 = Soil Moisture Sensor
  Componente3 = Soil Moisture Sensor

nets:
  N1: Componente1.B10, Componente3.SIG
  N2: Componente1.3V3, Mod1.pin1
  N3: Componente1.GND, Mod1.pin4
  GND: Componente1.GND3, RHT1.GND_1, Bauteil4.EOC, Componente2.GND, Componente3.GND
  5V: Componente1.5V, RHT1.Vcc, Bauteil4.XCLR
  N4: Componente1.B7, Bauteil4.VCC
  N5: Componente1.B6, Bauteil4.GND
  N6: Componente1.A10, Mod1.pin3#3
  N7: Componente1.A9, Mod1.pin3#2
  N8: Componente1.B12, RHT1.Data-signal
  N9: Componente1.B1, Componente2.SIG
  VCC: Componente2.VCC, Componente3.VCC

notes:
  A partire da sinistra
  VDD: 3.3V
  RST:
  RXD: PA9
  TXD: PA10
  GND: GND
  A partire da sinistra
  VCC: 5V
  GND: GND
  SCL: PB6
  SDA: PB7

custom parts:
  RYLR896: RYLR896 UART Interface 868/915mhz LORA Transceiver Module
